# Fritzing sketch sketch earthquake sensor (saved by Fritzing 0.9.3b)
breadboards: 1

parts:
  YwRobot_Power_Supply1 = YwRobot Breadboard Power Supply [part_number=545043]
  DFPlayer_Mini1 = DFPlayer MINI [package="DIP (Dual Inline) [THT]"]  # not connected
  LCM1602_IIC1 = LCM1602 IIC [part_number="LCM1602 IIC" chip_label="LCM1602 IIC" package="DIP (Dual Inline) [THT]"]
  AMP1 = GF1002 Stereo Amplifier
  Part1 = Passive Buzzer
  SP1 = SPEAKER [package=pcb_mount_speaker]
  Part2 = Arduino Nano (Rev3.0)
  LCD1 = LCD screen
  Part3 = Adafruit ADXL335 [part_number="Adafruit #163"]
  LED1 = smd LED [color="Red (633nm)" package="0603 [SMD]"]
  R2 = Resistor [tolerance=±5% resistance=10k package="0603 [SMD]"]
  S1 = Momentary Switch [package=ksa_sealed_tac_switch]
  S2 = Momentary Switch [package=ksa_sealed_tac_switch]
  R3 = Resistor [tolerance=±5% resistance=220 package="0805 [SMD]"]
  R4 = Resistor [tolerance=±5% resistance=1k package="0805 [SMD]"]
  R5 = Resistor [tolerance=±5% resistance=220 package="0805 [SMD]"]

nets:
  N1: YwRobot_Power_Supply1.VCC#5, S1.1, S1.2, S2.1, S2.2
  N2: YwRobot_Power_Supply1.VCC#9, LCM1602_IIC1.VCC, AMP1.POWER+
  N3: YwRobot_Power_Supply1.GND#11, Part1.GND, R4.Pin_0
  GND: YwRobot_Power_Supply1.GND#13, LCM1602_IIC1.GND, AMP1.POWER-, Part3.GND
  VSS: LCM1602_IIC1.VSS, LCD1.VSS
  VDD: LCM1602_IIC1.VDD, LCD1.VDD
  N4: LCM1602_IIC1.V0, LCD1.V0
  N5: LCM1602_IIC1.RS, LCD1.RS
  N6: LCM1602_IIC1.RW, LCD1.R/W
  N7: LCM1602_IIC1.E, LCD1.E
  N8: LCM1602_IIC1.D0, LCD1.DB0
  N9: LCM1602_IIC1.D1, LCD1.DB1
  N10: LCM1602_IIC1.D2, LCD1.DB2
  N11: LCM1602_IIC1.D3, LCD1.DB3
  N12: LCM1602_IIC1.D4, LCD1.DB4
  N13: LCM1602_IIC1.D5, LCD1.DB5
  N14: LCM1602_IIC1.D6, LCD1.DB6
  N15: LCM1602_IIC1.D7, LCD1.DB7
  N16: LCM1602_IIC1.A, LCD1.LED+
  N17: LCM1602_IIC1.K, LCD1.LED-
  N18: LCM1602_IIC1.SDA, Part2.A4
  N19: LCM1602_IIC1.SCL, Part2.A5
  N20: AMP1.ROUT-, SP1.+
  N21: AMP1.ROUT+, SP1.-
  N22: Part1.S, Part2.D8
  N23: Part2.D2, R5.Pin_0
  N24: Part2.D3, R3.Pin_0
  N25: Part2.D6, R2.Pin_1
  N26: Part2.D12/MISO, LED1.anode
  N27: Part2.A3, Part3.ZOUT
  N28: Part2.A2, Part3.YOUT
  N29: Part2.A1, Part3.XOUT
  N30: LED1.cathode, R4.Pin_1
  N31: S1.3, S1.4, R5.Pin_1
  N32: S2.3, S2.4, R3.Pin_1

custom parts:
  YwRobot Breadboard Power Supply: The YwRobot Breadboard Power Supply (MB-V2) has two power rails; they can be 5V or 3V3. Power to the module can be provided through the female USB socket or through the A10 (female) 2.1mm power jack.
  DFPlayer MINI: MP3 module by DFRobot.com for playing Music from an SD-Card. Supports WAV and MP3 files.
  LCM1602 IIC: I2C-Module to use a 1602 or 2004 LCD on with the wire.h libory Serial LCD Modul
  GF1002 Stereo Amplifier: GF1002 6 Watt Stereo Amplifier
  Adafruit ADXL335: We've updated our favorite triple-axis accelerometer to now have an on-board 3.3V regulator - making it a perfect choice for interfacing with a 5V microcontroller such as the Arduino. This breakout comes with 3 analog outputs for X, Y and Z axis measurements on a 0.75"x0.75" breakout board. The ADXL335 is the latest and greatest from Analog Devices, known for their exceptional quality MEMS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
